// Logisim project 1.1.b_7-Segment_ctl.circ as structural Verilog: 5 circuits, main circuit main
module main (
  input  in_1,
  input  in_2,
  input  in_3,
  input  in_4
);

  wire [15:0] decoder_4to16_1_y;

  Decoder_4to16 decoder_4to16_1 (.A3(in_1), .A2(in_2), .A1(in_3), .A0(in_4), .Y(decoder_4to16_1_y));
  _7_Segment_Display u_7_segment_display_1 ();  // open: g, f, a, b, e, d, c, dp
endmodule

module Decoder_2to4 (
  input  A1,
  input  A0,
  output Y3,
  output Y2,
  output Y1,
  output Y0
);

  wire not_1_out, not_2_out;

  not not_1 (not_1_out, A1);
  not not_2 (not_2_out, A0);
  and and_1 (Y3, A1, A0);
  and and_2 (Y2, A1, not_2_out);
  and and_3 (Y1, not_1_out, A0);
  and and_4 (Y0, not_1_out, not_2_out);
endmodule

module Decoder_3to8 (
  input  A2,
  input  A1,
  input  A0,
  output Y7,
  output Y6,
  output Y5,
  output Y4,
  output Y3,
  output Y2,
  output Y1,
  output Y0
);

  wire decoder_2to4_1_y0, decoder_2to4_1_y1, decoder_2to4_1_y2, decoder_2to4_1_y3, decoder_2to4_2_y0,
       decoder_2to4_2_y1, decoder_2to4_2_y2, decoder_2to4_2_y3, not_1_out;

  not not_1 (not_1_out, A2);
  Decoder_2to4 decoder_2to4_1 (
    .A1(A1), .A0(A0), .Y3(decoder_2to4_1_y3), .Y2(decoder_2to4_1_y2), .Y1(decoder_2to4_1_y1),
    .Y0(decoder_2to4_1_y0));
  Decoder_2to4 decoder_2to4_2 (
    .A1(A1), .A0(A0), .Y3(decoder_2to4_2_y3), .Y2(decoder_2to4_2_y2), .Y1(decoder_2to4_2_y1),
    .Y0(decoder_2to4_2_y0));
  and and_1 (Y7, decoder_2to4_1_y3, A2);
  and and_2 (Y6, decoder_2to4_1_y2, A2);
  and and_3 (Y5, decoder_2to4_1_y1, A2);
  and and_4 (Y4, decoder_2to4_1_y0, A2);
  and and_5 (Y3, decoder_2to4_2_y3, not_1_out);
  and and_6 (Y2, decoder_2to4_2_y2, not_1_out);
  and and_7 (Y1, decoder_2to4_2_y1, not_1_out);
  and and_8 (Y0, decoder_2to4_2_y0, not_1_out);
endmodule

module Decoder_4to16 (
  input  A3,
  input  A2,
  input  A1,
  input  A0,
  output [15:0] Y
);

  wire [7:0] decoder_3to8_1_y0, decoder_3to8_2_y0;
  wire [7:7] not_1_out;

  not not_1 (not_1_out[7], A3);
  Decoder_3to8 decoder_3to8_1 (
    .A2(A2), .A1(A1), .A0(A0), .Y7(decoder_3to8_1_y0[7]), .Y6(decoder_3to8_1_y0[6]),
    .Y5(decoder_3to8_1_y0[5]), .Y4(decoder_3to8_1_y0[4]), .Y3(decoder_3to8_1_y0[3]),
    .Y2(decoder_3to8_1_y0[2]), .Y1(decoder_3to8_1_y0[1]), .Y0(decoder_3to8_1_y0[0]));
  Decoder_3to8 decoder_3to8_2 (
    .A2(A2), .A1(A1), .A0(A0), .Y7(decoder_3to8_2_y0[7]), .Y6(decoder_3to8_2_y0[6]),
    .Y5(decoder_3to8_2_y0[5]), .Y4(decoder_3to8_2_y0[4]), .Y3(decoder_3to8_2_y0[3]),
    .Y2(decoder_3to8_2_y0[2]), .Y1(decoder_3to8_2_y0[1]), .Y0(decoder_3to8_2_y0[0]));
  assign Y[15:8] = {8{A3}} & decoder_3to8_1_y0;  // AND_Gate and_1, 8 bits wide
  assign Y[7:0] = decoder_3to8_2_y0 & {8{not_1_out[7]}};  // AND_Gate and_2, 8 bits wide
endmodule

module Seg_ctl (
  input  a,
  input  b,
  output c
);

  and and_1 (c, a, b);
endmodule
