// Logisim project 1.3.2_sim_d-latch_rstn.circ as structural Verilog: 3 circuits, main circuit sim
module sim (
  input  in_1,
  input  in_2
);

  wire d_latch_1_q, not_1_out;

  d_latch d_latch_1 (.D(not_1_out), .WE(in_1), .rstn(in_2), .Q(d_latch_1_q));
  not not_1 (not_1_out, d_latch_1_q);
  LED led_1 (.in(not_1_out));
endmodule

module d_latch (
  input  D,
  input  WE,
  input  rstn,
  output Q
);

  wire and_1_out, and_2_out, not_1_out, sr_latch_1_q;

  not not_1 (not_1_out, D);
  and and_1 (and_1_out, D, WE);
  and and_2 (and_2_out, WE, not_1_out);
  sr_latch sr_latch_1 (.R(and_2_out), .S(and_1_out), .Q(sr_latch_1_q));  // open: Qn
  and and_3 (Q, rstn, sr_latch_1_q);
endmodule

module sr_latch (
  input  R,
  input  S,
  output Q,
  output Qn
);

  nor nor_1 (Q, R, Qn);
  nor nor_2 (Qn, Q, S);
endmodule
