// Logisim project full_adder_4bit.circ as structural Verilog: 1 circuit, main circuit x_full_adder_4bit
module x_full_adder_4bit (
  input  a3,
  input  a2,
  input  a1,
  input  a0,
  input  b3,
  input  b2,
  input  b1,
  input  b0,
  input  cin,
  output s3,
  output s2,
  output s1,
  output s0,
  output cout
);

  wire full_adder_1bit_2_cout, full_adder_1bit_3_cout, full_adder_1bit_4_cout;

  full_adder_1bit full_adder_1bit_1 (.a(a3), .b(b3), .cin(full_adder_1bit_2_cout), .s(s3), .cout(cout));
  full_adder_1bit full_adder_1bit_2 (
    .a(a2), .b(b2), .cin(full_adder_1bit_3_cout), .s(s2), .cout(full_adder_1bit_2_cout));
  full_adder_1bit full_adder_1bit_3 (
    .a(a1), .b(b1), .cin(full_adder_1bit_4_cout), .s(s1), .cout(full_adder_1bit_3_cout));
  full_adder_1bit full_adder_1bit_4 (.a(a0), .b(b0), .cin(cin), .s(s0), .cout(full_adder_1bit_4_cout));
endmodule
