// Logisim project full_sub_4bit.circ as structural Verilog: 2 circuits, main circuit full_sub_1bit
module full_sub_4bit (
  input  a3,
  input  a2,
  input  a1,
  input  a0,
  input  b3,
  input  b2,
  input  b1,
  input  b0,
  input  cin,
  output d3,
  output d2,
  output d1,
  output d0,
  output cout
);

  wire full_sub_1bit_2_cout, full_sub_1bit_3_cout, full_sub_1bit_4_cout;

  full_sub_1bit full_sub_1bit_1 (.a(a3), .b(b3), .cin(full_sub_1bit_2_cout), .d(d3), .cout(cout));
  full_sub_1bit full_sub_1bit_2 (.a(a2), .b(b2), .cin(full_sub_1bit_3_cout), .d(d2), .cout(full_sub_1bit_2_cout));
  full_sub_1bit full_sub_1bit_3 (.a(a1), .b(b1), .cin(full_sub_1bit_4_cout), .d(d1), .cout(full_sub_1bit_3_cout));
  full_sub_1bit full_sub_1bit_4 (.a(a0), .b(b0), .cin(cin), .d(d0), .cout(full_sub_1bit_4_cout));
endmodule

module full_sub_1bit (
  input  a,
  input  b,
  input  cin,
  output d,
  output cout
);

  wire and_1_out, and_2_out, not_1_out, not_2_out, xor_1_out;

  xor xor_1 (xor_1_out, a, b);
  not not_1 (not_1_out, a);
  not not_2 (not_2_out, xor_1_out);
  xor xor_2 (d, xor_1_out, cin);
  and and_1 (and_1_out, not_2_out, cin);
  and and_2 (and_2_out, not_1_out, b);
  or or_1 (cout, and_1_out, and_2_out);
endmodule
